# Fritzing sketch servo-sketch (saved by Fritzing 0.9.3b)
breadboards: 1

parts:
  Part1 = Arduino Uno (Rev3)
  S1 = Pushbutton [package="[THT]"]
  S2 = Pushbutton [package="[THT]"]
  LED1 = LED - 5mm [color="Green (560nm)" package="5 mm [THT]"]
  R1 = Resistor [tolerance=±5% resistance=220 package="0402 [SMD]"]
  LED2 = LED - 5mm [color="Red (635nm)" package="5 mm [THT]"]
  R2 = Resistor [tolerance=±5% resistance=220 package="0402 [SMD]"]
  J1 = Basic Servo
  S3 = Pushbutton [package="[THT]"]
  U3 = POT [package=pot_mammoth]

nets:
  N1: Part1.A0, U3.A
  N2: Part1.D9_PWM, J1.pulse
  N3: Part1.D12/MISO, LED2.anode
  N4: Part1.D13/SCK, LED1.anode
  N5: Part1.D5_PWM, S3.Pin_1, S3.Pin_2
  N6: Part1.D6_PWM, S1.Pin_3, S1.Pin_4
  N7: Part1.D7, S2.Pin_1, S2.Pin_2
  5V: Part1.5V, J1.vcc, U3.S
  GND: Part1.GND, S1.Pin_1, S1.Pin_2, S2.Pin_3, S2.Pin_4, J1.gnd, S3.Pin_3, S3.Pin_4, U3.E
  N8: LED1.cathode, R1.Pin_1
  N9: LED2.cathode, R2.Pin_1
